# Fritzing sketch AD2Check (saved by Fritzing 0.8.3b)
circuit board: 4.3cm x 1.5cm
breadboards: 1

parts:
  J2 = female pin header, 15 pins [form="♀ (female)"]
  J1 = female pin header, 15 pins [form="♀ (female)"]
  J3 = female pin header, 1 pin [form="♀ (female)"]
  J4 = female pin header, 1 pin [form="♀ (female)"]
  J5 = female pin header, 1 pin [form="♀ (female)"]
  J6 = female pin header, 1 pin [form="♀ (female)"]

nets:
  N1: J2.pin1, J2.pin5
  N2: J2.pin2, J2.pin4
  N3: J2.pin8, J1.pin8
  N4: J2.pin9, J1.pin9
  N5: J2.pin10, J1.pin10
  N6: J2.pin11, J1.pin11
  N7: J2.pin12, J1.pin12
  N8: J2.pin13, J1.pin13
  N9: J2.pin14, J1.pin14
  N10: J2.pin15, J1.pin15
  N11: J1.pin1, J1.pin2, J1.pin3
  N12: J3.pin1, J4.pin1, J5.pin1, J6.pin1
