# Fritzing sketch AD2CheckWSw3018 (saved by Fritzing 0.8.3b)
circuit board: 7cm x 10cm
breadboards: 1

parts:
  V+ = male pin header, 3 pins [form="♂ (male)"]
  W1 = male pin header, 3 pins [form="♂ (male)"]
  Jump = male pin header, 3 pins [form="♂ (male)"]
  Jump_2 = male pin header, 3 pins [form="♂ (male)"]
  D7 = female pin header, 15 pins [form="♀ (female)"]
  1- = female pin header, 15 pins [form="♀ (female)"]
  W3 = male pin header, 3 pins [form="♂ (male)"]
  V+2 = male pin header, 3 pins [form="♂ (male)"]
  Jump3 = male pin header, 3 pins [form="♂ (male)"]
  Jump5 = male pin header, 3 pins [form="♂ (male)"]
  D9 = female pin header, 15 pins [form="♀ (female)"]
  1-2 = female pin header, 15 pins [form="♀ (female)"]
  W5 = male pin header, 3 pins [form="♂ (male)"]
  V+4 = male pin header, 3 pins [form="♂ (male)"]
  Jump7 = male pin header, 3 pins [form="♂ (male)"]
  Jump9 = male pin header, 3 pins [form="♂ (male)"]
  D11 = female pin header, 15 pins [form="♀ (female)"]
  1-4 = female pin header, 15 pins [form="♀ (female)"]

nets:
  N1: V+.pin1, Jump.pin1, D7.pin12
  N2: V+.pin2, Jump.pin2, D7.pin14
  N3: V+.pin3, Jump.pin3, 1-.pin12
  N4: W1.pin1, Jump_2.pin1, D7.pin11
  N5: W1.pin2, Jump_2.pin2, D7.pin15
  N6: W1.pin3, Jump_2.pin3, 1-.pin11
  N7: D7.pin1, 1-.pin1
  N8: D7.pin2, 1-.pin2
  N9: D7.pin3, 1-.pin3
  N10: D7.pin4, 1-.pin4
  N11: D7.pin5, 1-.pin5
  N12: D7.pin6, 1-.pin6
  N13: D7.pin7, 1-.pin7
  N14: D7.pin8, 1-.pin8
  N15: D7.pin13, 1-.pin13, 1-.pin14, 1-.pin15
  N16: W3.pin1, Jump5.pin1
  N17: W3.pin2, Jump5.pin2, D9.pin15
  N18: W3.pin3, Jump5.pin3, 1-2.pin11
  N19: V+2.pin1, Jump3.pin1, D9.pin12
  N20: V+2.pin2, Jump3.pin2, D9.pin14
  N21: V+2.pin3, Jump3.pin3, 1-2.pin12
  N22: D9.pin1, 1-2.pin1
  N23: D9.pin2, 1-2.pin2
  N24: D9.pin3, 1-2.pin3
  N25: D9.pin4, 1-2.pin4
  N26: D9.pin5, 1-2.pin5
  N27: D9.pin6, 1-2.pin6
  N28: D9.pin7, 1-2.pin7
  N29: D9.pin8, 1-2.pin8
  N30: D9.pin13, 1-2.pin13, 1-2.pin14, 1-2.pin15
  N31: W5.pin1, Jump9.pin1, D11.pin11
  N32: W5.pin2, Jump9.pin2, D11.pin15
  N33: W5.pin3, Jump9.pin3, 1-4.pin11
  N34: V+4.pin1, Jump7.pin1, D11.pin12
  N35: V+4.pin2, Jump7.pin2, D11.pin14
  N36: V+4.pin3, Jump7.pin3, 1-4.pin12
  N37: D11.pin1, 1-4.pin1
  N38: D11.pin2, 1-4.pin2
  N39: D11.pin3, 1-4.pin3
  N40: D11.pin4, 1-4.pin4
  N41: D11.pin5, 1-4.pin5
  N42: D11.pin6, 1-4.pin6
  N43: D11.pin7, 1-4.pin7
  N44: D11.pin8, 1-4.pin8
  N45: D11.pin13, 1-4.pin13, 1-4.pin14, 1-4.pin15

notes:
  V-
  W2
  V+
  W1
  Jump
