# Fritzing sketch Untitled Sketch 3 (saved by Fritzing 0.8.3b)
circuit board: 9.9cm x 9.9cm
breadboards: 1

parts:
  V+ = male pin header, 3 pins [form="♂ (male)"]
  W1 = male pin header, 3 pins [form="♂ (male)"]
  Jump = male pin header, 3 pins [form="♂ (male)"]
  Jump_2 = male pin header, 3 pins [form="♂ (male)"]
  D7 = female pin header, 15 pins [form="♀ (female)"]
  1- = female pin header, 15 pins [form="♀ (female)"]
  W2 = male pin header, 3 pins [form="♂ (male)"]
  V+1 = male pin header, 3 pins [form="♂ (male)"]
  Jump1 = male pin header, 3 pins [form="♂ (male)"]
  Jump2 = male pin header, 3 pins [form="♂ (male)"]
  D8 = female pin header, 15 pins [form="♀ (female)"]
  1-1 = female pin header, 15 pins [form="♀ (female)"]
  W3 = male pin header, 3 pins [form="♂ (male)"]
  V+2 = male pin header, 3 pins [form="♂ (male)"]
  Jump3 = male pin header, 3 pins [form="♂ (male)"]
  Jump4 = male pin header, 3 pins [form="♂ (male)"]
  Jump5 = male pin header, 3 pins [form="♂ (male)"]
  Jump6 = male pin header, 3 pins [form="♂ (male)"]
  D9 = female pin header, 15 pins [form="♀ (female)"]
  D10 = female pin header, 15 pins [form="♀ (female)"]
  1-2 = female pin header, 15 pins [form="♀ (female)"]
  1-3 = female pin header, 15 pins [form="♀ (female)"]
  W4 = male pin header, 3 pins [form="♂ (male)"]
  V+3 = male pin header, 3 pins [form="♂ (male)"]
  W5 = male pin header, 3 pins [form="♂ (male)"]
  V+4 = male pin header, 3 pins [form="♂ (male)"]
  Jump7 = male pin header, 3 pins [form="♂ (male)"]
  Jump8 = male pin header, 3 pins [form="♂ (male)"]
  Jump9 = male pin header, 3 pins [form="♂ (male)"]
  Jump10 = male pin header, 3 pins [form="♂ (male)"]
  D11 = female pin header, 15 pins [form="♀ (female)"]
  D12 = female pin header, 15 pins [form="♀ (female)"]
  1-4 = female pin header, 15 pins [form="♀ (female)"]
  1-5 = female pin header, 15 pins [form="♀ (female)"]
  W6 = male pin header, 3 pins [form="♂ (male)"]
  V+5 = male pin header, 3 pins [form="♂ (male)"]

nets:
  N1: V+.pin1, Jump.pin1, D7.pin12
  N2: V+.pin2, Jump.pin2, D7.pin14
  N3: V+.pin3, Jump.pin3, 1-.pin12
  N4: W1.pin1, Jump_2.pin1, D7.pin11
  N5: W1.pin2, Jump_2.pin2, D7.pin15
  N6: W1.pin3, Jump_2.pin3, 1-.pin11
  N7: D7.pin1, 1-.pin1
  N8: D7.pin2, 1-.pin2
  N9: D7.pin3, 1-.pin3
  N10: D7.pin4, 1-.pin4
  N11: D7.pin5, 1-.pin5
  N12: D7.pin6, 1-.pin6
  N13: D7.pin7, 1-.pin7
  N14: D7.pin8, 1-.pin8
  N15: D7.pin13, 1-.pin13, 1-.pin14, 1-.pin15
  N16: W2.pin1, Jump2.pin1, D8.pin11
  N17: W2.pin2, Jump2.pin2, D8.pin15
  N18: W2.pin3, Jump2.pin3, 1-1.pin11
  N19: V+1.pin1, Jump1.pin1, D8.pin12
  N20: V+1.pin2, Jump1.pin2, D8.pin14
  N21: V+1.pin3, Jump1.pin3, 1-1.pin12
  N22: D8.pin1, 1-1.pin1
  N23: D8.pin2, 1-1.pin2
  N24: D8.pin3, 1-1.pin3
  N25: D8.pin4, 1-1.pin4
  N26: D8.pin5, 1-1.pin5
  N27: D8.pin6, 1-1.pin6
  N28: D8.pin7, 1-1.pin7
  N29: D8.pin8, 1-1.pin8
  N30: D8.pin13, 1-1.pin13, 1-1.pin14, 1-1.pin15
  N31: W3.pin1, Jump5.pin1
  N32: W3.pin2, Jump5.pin2, D9.pin15
  N33: W3.pin3, Jump5.pin3, 1-2.pin11
  N34: V+2.pin1, Jump3.pin1, D9.pin12
  N35: V+2.pin2, Jump3.pin2, D9.pin14
  N36: V+2.pin3, Jump3.pin3, 1-2.pin12
  N37: Jump4.pin1, D10.pin12, V+3.pin1
  N38: Jump4.pin2, D10.pin14, V+3.pin2
  N39: Jump4.pin3, 1-3.pin12, V+3.pin3
  N40: Jump6.pin1, D10.pin11, W4.pin1
  N41: Jump6.pin2, D10.pin15, W4.pin2
  N42: Jump6.pin3, 1-3.pin11, W4.pin3
  N43: D9.pin1, 1-2.pin1
  N44: D9.pin2, 1-2.pin2
  N45: D9.pin3, 1-2.pin3
  N46: D9.pin4, 1-2.pin4
  N47: D9.pin5, 1-2.pin5
  N48: D9.pin6, 1-2.pin6
  N49: D9.pin7, 1-2.pin7
  N50: D9.pin8, 1-2.pin8
  N51: D9.pin13, 1-2.pin13, 1-2.pin14, 1-2.pin15
  N52: D10.pin1, 1-3.pin1
  N53: D10.pin2, 1-3.pin2
  N54: D10.pin3, 1-3.pin3
  N55: D10.pin4, 1-3.pin4
  N56: D10.pin5, 1-3.pin5
  N57: D10.pin6, 1-3.pin6
  N58: D10.pin7, 1-3.pin7
  N59: D10.pin8, 1-3.pin8
  N60: D10.pin13, 1-3.pin13, 1-3.pin14, 1-3.pin15
  N61: W5.pin1, Jump9.pin1, D11.pin11
  N62: W5.pin2, Jump9.pin2, D11.pin15
  N63: W5.pin3, Jump9.pin3, 1-4.pin11
  N64: V+4.pin1, Jump7.pin1, D11.pin12
  N65: V+4.pin2, Jump7.pin2, D11.pin14
  N66: V+4.pin3, Jump7.pin3, 1-4.pin12
  N67: Jump8.pin1, D12.pin12, V+5.pin1
  N68: Jump8.pin2, D12.pin14, V+5.pin2
  N69: Jump8.pin3, 1-5.pin12, V+5.pin3
  N70: Jump10.pin1, D12.pin11, W6.pin1
  N71: Jump10.pin2, D12.pin15, W6.pin2
  N72: Jump10.pin3, 1-5.pin11, W6.pin3
  N73: D11.pin1, 1-4.pin1
  N74: D11.pin2, 1-4.pin2
  N75: D11.pin3, 1-4.pin3
  N76: D11.pin4, 1-4.pin4
  N77: D11.pin5, 1-4.pin5
  N78: D11.pin6, 1-4.pin6
  N79: D11.pin7, 1-4.pin7
  N80: D11.pin8, 1-4.pin8
  N81: D11.pin13, 1-4.pin13, 1-4.pin14, 1-4.pin15
  N82: D12.pin1, 1-5.pin1
  N83: D12.pin2, 1-5.pin2
  N84: D12.pin3, 1-5.pin3
  N85: D12.pin4, 1-5.pin4
  N86: D12.pin5, 1-5.pin5
  N87: D12.pin6, 1-5.pin6
  N88: D12.pin7, 1-5.pin7
  N89: D12.pin8, 1-5.pin8
  N90: D12.pin13, 1-5.pin13, 1-5.pin14, 1-5.pin15

notes:
  V-
  W2
  V+
  W1
  Jump
